// Logisim project drisc.circ as structural Verilog: 16 circuits, main circuit main
module main (
  input  in_1
);

  wire Addr_ALU_Use_PC, Alu_Read, ALU_Use_PC, button_1_out, Cl0ck, IO_Load, IO_Read_IO, IO_Write_IO,
       keyboard_1_avail, Load_Upper_Immediate, MemoryController_read_keyboard, MemoryController_readram,
       MemoryController_write_video, MemoryController_writeram, not_2_out, OperationController_pad_read,
       OperationController_pad_read_address, OperationController_pad_write, P2_out, PC_Jump, PC_Read_Next,
       PC_Use_Offset, Phase1, Phase3, Register_File_Write, Reset, Send_Address, Shifter_Read, Use_Immediate;
  wire [1:0] Data_Offset, MemoryController_address_out_24bit, OperationController_pad_data_size;
  wire [2:0] Funct3;
  wire [3:0] ALUComponent_cnzv;
  wire [4:0] OP_Function;
  wire [6:0] keyboard_1_data, keyboard_2_data, OperationController_opcode;
  wire [7:0] controlled_buffer_1_out, controlled_buffer_1_out_2, controlled_buffer_1_out_3,
       controlled_buffer_1_out_4;
  wire [7:7] not_1_out;
  wire [14:0] Register_Addresses;
  wire [21:0] MemoryController_address_out_24bit_2;
  wire [31:0] AddressALU_result, ALUComponent_result, DataIO_cpu_out, DataIO_io_out, Immediate,
       MemoryController_addressdebug, multiplexer_1_out, multiplexer_2_out, multiplexer_3_out,
       multiplexer_4_out, ProgramCounter_p9, ProgramCounter_p10, ProgramCounter_p11, RegisterFile_a_bus_out,
       RegisterFile_b_bus_out, Shifter_c_bus_out;

  // Probe on Register_Addresses[4:0]
  // Probe on Register_Addresses[9:5]
  // Probe on Register_Addresses[14:10]
  Register_File RegisterFile (
    .C_Bus_In(multiplexer_1_out), .Addresses_In(Register_Addresses), .Write(Register_File_Write),
    .Clock(Cl0ck), .Reset(Reset), .A_Bus_Out(RegisterFile_a_bus_out), .B_Bus_Out(RegisterFile_b_bus_out));
  // Probe on RegisterFile_a_bus_out
  // Probe on RegisterFile_b_bus_out
  // Probe on multiplexer_1_out
  assign {controlled_buffer_1_out_4, controlled_buffer_1_out_3, controlled_buffer_1_out_2, controlled_buffer_1_out} = IO_Read_IO ? DataIO_io_out : 32'bz;  // Controlled_Buffer controlled_buffer_1
  Multiplexer #(.width(32)) multiplexer_1 (
    .in0(multiplexer_2_out), .in1(DataIO_cpu_out), .out(multiplexer_1_out), .sel(IO_Load));
  Data_Input_Output DataIO (
    .Store_CPU(Phase1),
    .IO_In({controlled_buffer_1_out_4, controlled_buffer_1_out_3, controlled_buffer_1_out_2, controlled_buffer_1_out}),
    .Write_IO(IO_Write_IO), .Clock(Cl0ck), .Data_Offset(Data_Offset), .Data_Type(Funct3),
    .CPU_In(RegisterFile_b_bus_out), .CPU_Out(DataIO_cpu_out), .IO_Out(DataIO_io_out));
  Multiplexer #(.width(32)) multiplexer_2 (
    .in0(multiplexer_3_out), .in1(Immediate), .out(multiplexer_2_out), .sel(Load_Upper_Immediate));
  Shifter_Circuit Shifter (
    .Select_Immediate(Use_Immediate), .B_Bus_In(RegisterFile_b_bus_out), .Immediate_In(Immediate),
    .A_Bus_In(RegisterFile_a_bus_out), .Clock(Cl0ck), .Write(Phase1), .Operation_Select(OP_Function),
    .C_Bus_Out(Shifter_c_bus_out));
  Multiplexer #(.width(32)) multiplexer_3 (
    .in0(multiplexer_4_out), .in1(Shifter_c_bus_out), .out(multiplexer_3_out), .sel(Shifter_Read));
  ALU ALUComponent (
    .Use_PC(ALU_Use_PC), .Use_Immediate(Use_Immediate), .Write(Phase1), .Source1(RegisterFile_a_bus_out),
    .Program_Counter_In(ProgramCounter_p11), .Source2(RegisterFile_b_bus_out), .Immediate(Immediate),
    .Clock(Cl0ck), .Operation(OP_Function), .Result(ALUComponent_result), .CNZV(ALUComponent_cnzv));
  Multiplexer #(.width(32)) multiplexer_4 (
    .in0(ALUComponent_result), .in1(ProgramCounter_p10), .out(multiplexer_4_out), .sel(PC_Read_Next));
  Clock #(.highDuration(2), .lowDuration(4), .phaseOffset(5)) P1 (.out(Phase1));
  Clock #(.highDuration(2), .lowDuration(4), .phaseOffset(3)) P2 (.out(P2_out));
  Clock #(.highDuration(2), .lowDuration(4), .phaseOffset(1)) P3 (.out(Phase3));
  // Probe on Immediate
  Operation_Controller OperationController (
    .Phase1(Phase1), .Phase2(P2_out), .Phase3(Phase3), .CNZV(ALUComponent_cnzv), .Clock(Cl0ck),
    .Reset(Reset),
    .Data_In({controlled_buffer_1_out_4, controlled_buffer_1_out_3, controlled_buffer_1_out_2, controlled_buffer_1_out}),
    .OPCode(OperationController_opcode), .Register_Adresses(Register_Addresses), .Funct3(Funct3),
    .Immediate(Immediate), .PC_Use_Offset(PC_Use_Offset), .PC_Addr_In_to_AD(Send_Address),
    .Register_File_Write(Register_File_Write), .PC_Read_Next(PC_Read_Next),
    .Load_Upper_Immediate(Load_Upper_Immediate), .Alu_Read(Alu_Read), .PC_Jump(PC_Jump),
    .Use_Immediate(Use_Immediate), .OP_Function(OP_Function), .Address_ALU_Use_PC(Addr_ALU_Use_PC),
    .ALU_Use_PC(ALU_Use_PC), .PAD_Read_Address(OperationController_pad_read_address),
    .Shifter_Read(Shifter_Read), .Data_IO_Write_IO(IO_Write_IO), .PAD_Read(OperationController_pad_read),
    .Data_IO_Read_IO(IO_Read_IO), .PAD_Data_Size(OperationController_pad_data_size),
    .PAD_Write(OperationController_pad_write), .IO_Load(IO_Load));
  // Probe on OperationController_opcode
  Address_ALU AddressALU (
    .Clock(Cl0ck), .Use_PC(Addr_ALU_Use_PC), .Source1(RegisterFile_a_bus_out),
    .Program_Counter_In(ProgramCounter_p11), .Immediate(Immediate), .Write(Phase1), .Result(AddressALU_result));
  // Probe on ProgramCounter_p11
  // Program_Counter ProgramCounter: pin names not known; wires that end beside it: Send_Address, Phase3, PC_Jump, PC_Use_Offset, AddressALU_result, Data_Offset, Reset, Cl0ck, ProgramCounter_p9, ProgramCounter_p10, ProgramCounter_p11
  // Probe on {controlled_buffer_1_out_4, controlled_buffer_1_out_3, controlled_buffer_1_out_2, controlled_buffer_1_out}
  // Probe on ProgramCounter_p9
  Clock MainClock (.out(Cl0ck));
  POR #(.PorHighDuration(1), .porsize(2)) por_1 (.out(Reset));
  // Probe on MemoryController_addressdebug
  IO_Controller MemoryController (
    .Write_Address(OperationController_pad_read_address), .Clock(Cl0ck), .Address_In(ProgramCounter_p9),
    .Reset(Reset), .Keyboard_Address(32'h7fe), .Video_Address(32'h7ff),
    .Write(OperationController_pad_write), .Read(OperationController_pad_read),
    .Address_Out_24Bit({MemoryController_address_out_24bit_2, MemoryController_address_out_24bit}),
    .AddressDebug(MemoryController_addressdebug), .Read_Keyboard(MemoryController_read_keyboard),
    .Write_Video(MemoryController_write_video), .WriteRam(MemoryController_writeram),
    .ReadRam(MemoryController_readram));  // open: Rom_Address_Out_8Bit, Write_OS_Ram, Read_OS_Ram
  // Shift_Register #(.length(64), .trigger("falling"), .width(22)) shift_register_1: pin names not known; wires that end beside it: Cl0ck, MemoryController_address_out_24bit_2
  // Buffer buffer_1 has open pins: in=MemoryController_writeram, out=open
  // RAM #(.addrWidth(24), .databus("bidir"), .enables("line"), .line("quad"), .misaligned("true"), .trigger("falling"), .\type ("nonvolatile")) ram_1: pin names not known; wires that end beside it: {MemoryController_address_out_24bit_2, MemoryController_address_out_24bit}, MemoryController_writeram, MemoryController_readram, 1'b1, OperationController_pad_data_size[1], Cl0ck
  Keyboard keyboard_1 (
    .clk(MemoryController_read_keyboard), .re(1'b1), .avail(keyboard_1_avail), .data(keyboard_1_data));  // open: clr
  // Probe on nothing
  // Probe on nothing
  // Probe on nothing
  // Probe on nothing
  // Probe on nothing
  // Probe on nothing
  // Probe on nothing
  // Probe on nothing
  // Probe on nothing
  // Probe on nothing
  // Probe on nothing
  // Probe on nothing
  // Probe on nothing
  // Probe on nothing
  // Probe on nothing
  // Probe on nothing
  // Probe on nothing
  // Probe on nothing
  // Probe on nothing
  // Probe on nothing
  // Probe on nothing
  // Probe on nothing
  // Probe on nothing
  // Probe on nothing
  // Probe on nothing
  // Probe on nothing
  // Probe on nothing
  // Probe on nothing
  // Probe on nothing
  // Probe on nothing
  // Probe on nothing
  // Probe on nothing
  // Probe on nothing
  // Probe on nothing
  // Probe on nothing
  // Probe on nothing
  // Probe on nothing
  // Probe on nothing
  // Probe on nothing
  // Probe on nothing
  // Probe on nothing
  // Probe on nothing
  // Probe on nothing
  // Probe on nothing
  // Probe on nothing
  // Probe on nothing
  // Probe on nothing
  // Probe on nothing
  // Probe on nothing
  // Probe on nothing
  // Probe on nothing
  // Probe on nothing
  // Probe on nothing
  // Probe on nothing
  // Probe on nothing
  // Probe on nothing
  // Probe on nothing
  // Probe on nothing
  // Probe on nothing
  // Probe on nothing
  // Probe on nothing
  // Probe on nothing
  // Probe on nothing
  // Probe on nothing
  // Shift_Register #(.length(64), .trigger("falling"), .width(22)) shift_register_2: pin names not known; wires that end beside it: Cl0ck, MemoryController_address_out_24bit_2
  // Buffer buffer_2 has open pins: in=MemoryController_readram, out=open
  not not_1 (not_1_out[7], keyboard_1_avail);
  assign {controlled_buffer_1_out_4, controlled_buffer_1_out_3, controlled_buffer_1_out_2, controlled_buffer_1_out} = MemoryController_read_keyboard ? {{24{1'b0}}, not_1_out[7], keyboard_1_data} : 32'bz;  // Controlled_Buffer controlled_buffer_2
  // Probe on nothing
  // Probe on nothing
  // Probe on nothing
  // Probe on nothing
  // Probe on nothing
  // Probe on nothing
  // Probe on nothing
  // Probe on nothing
  // Probe on nothing
  // Probe on nothing
  // Probe on nothing
  // Probe on nothing
  // Probe on nothing
  // Probe on nothing
  // Probe on nothing
  // Probe on nothing
  // Probe on nothing
  // Probe on nothing
  // Probe on nothing
  // Probe on nothing
  // Probe on nothing
  // Probe on nothing
  // Probe on nothing
  // Probe on nothing
  // Probe on nothing
  // Probe on nothing
  // Probe on nothing
  // Probe on nothing
  // Probe on nothing
  // Probe on nothing
  // Probe on nothing
  // Probe on nothing
  // Probe on nothing
  // Probe on nothing
  // Probe on nothing
  // Probe on nothing
  // Probe on nothing
  // Probe on nothing
  // Probe on nothing
  // Probe on nothing
  // Probe on nothing
  // Probe on nothing
  // Probe on nothing
  // Probe on nothing
  // Probe on nothing
  // Probe on nothing
  // Probe on nothing
  // Probe on nothing
  // Probe on nothing
  // Probe on nothing
  // Probe on nothing
  // Probe on nothing
  // Probe on nothing
  // Probe on nothing
  // Probe on nothing
  // Probe on nothing
  // Probe on nothing
  // Probe on nothing
  // Probe on nothing
  // Probe on nothing
  // Probe on nothing
  // Probe on nothing
  // Probe on nothing
  // Probe on nothing
  Button button_1 (.out(button_1_out));
  Keyboard keyboard_2 (.clk(button_1_out), .re(in_1), .data(keyboard_2_data));  // open: clr, avail
  not not_2 (not_2_out, Cl0ck);
  // RGB_Video #(.cursor("No Cursor"), .height(64), .reset("Synchronous"), .scale(6), .width(64)) rgb_video_1: pin names not known; wires that end beside it: controlled_buffer_1_out_4[7], not_2_out, MemoryController_write_video, {controlled_buffer_1_out_2[3:0], controlled_buffer_1_out[7:6]}, controlled_buffer_1_out[5:0], {controlled_buffer_1_out_4[3:0], controlled_buffer_1_out_3, controlled_buffer_1_out_2[7:4]}
  // Probe on keyboard_2_data

  // Notes on the sheet:
  //   <Processor     Input Output Devices>
  //   Data Bus
  //   (IO Bus)
  //   Address Bus
  //   (AD Bus)
endmodule

module Shifter_Circuit (
  input  Select_Immediate,
  input  [31:0] B_Bus_In,
  input  [31:0] Immediate_In,
  input  [4:0] Operation_Select,
  input  Write,
  input  [31:0] A_Bus_In,
  input  Clock,
  output [31:0] C_Bus_Out
);

  wire [4:0] multiplexer_1_out, Shift_Amount_Latch_q;
  wire [31:0] Shift_In_Latch_q, shifter_1_out, shifter_2_out, shifter_3_out;

  Multiplexer #(.width(5)) multiplexer_1 (
    .in0(B_Bus_In[4:0]), .in1(Immediate_In[4:0]), .out(multiplexer_1_out), .sel(Select_Immediate));
  Register #(.trigger("falling"), .width(5)) Shift_Amount_Latch (
    .D(multiplexer_1_out), .en(Write), .clk(Clock), .Q(Shift_Amount_Latch_q));  // open: clr
  Register #(.trigger("falling"), .width(32)) Shift_In_Latch (
    .D(A_Bus_In), .en(Write), .clk(Clock), .Q(Shift_In_Latch_q));  // open: clr
  Shifter #(.width(32)) shifter_1 (.in(Shift_In_Latch_q), .\dist (Shift_Amount_Latch_q), .out(shifter_1_out));
  Shifter #(.shift("lr"), .width(32)) shifter_2 (
    .in(Shift_In_Latch_q), .\dist (Shift_Amount_Latch_q), .out(shifter_2_out));
  Shifter #(.shift("ar"), .width(32)) shifter_3 (
    .in(Shift_In_Latch_q), .\dist (Shift_Amount_Latch_q), .out(shifter_3_out));
  Multiplexer #(.select(2), .width(32)) multiplexer_2 (
    .in0(shifter_1_out), .in1(shifter_2_out), .in2(shifter_3_out), .in3(shifter_3_out), .out(C_Bus_Out),
    .sel({Operation_Select[4], Operation_Select[2]}));
endmodule

module Address_ALU (
  input  Write,
  input  Use_PC,
  input  [31:0] Source1,
  input  [31:0] Program_Counter_In,
  input  [31:0] Immediate,
  input  Clock,
  output [31:0] Result
);

  wire not_1_out;
  wire [31:0] multiplexer_1_out, Source_1_q, Source_2_q;

  not not_1 (not_1_out, Clock);
  Multiplexer #(.width(32)) multiplexer_1 (
    .in0(Source1), .in1(Program_Counter_In), .out(multiplexer_1_out), .sel(Use_PC));
  Register #(.width(32)) Source_1 (.D(multiplexer_1_out), .en(Write), .clk(not_1_out), .Q(Source_1_q));  // open: clr
  Register #(.width(32)) Source_2 (.D(Immediate), .en(Write), .clk(not_1_out), .Q(Source_2_q));  // open: clr
  Adder #(.width(32)) adder_1 (.a(Source_1_q), .b(Source_2_q), .out(Result));  // open: cin, cout

  // Notes on the sheet:
  //   Source1: initial=0xffffffff
endmodule

module ALU (
  input  [4:0] Operation,
  input  Write,
  input  Use_PC,
  input  [31:0] Source1,
  input  [31:0] Program_Counter_In,
  input  Use_Immediate,
  input  [31:0] Source2,
  input  [31:0] Immediate,
  input  Clock,
  output [3:0] CNZV,
  output [31:0] Result
);

  wire comparator_1_lt, comparator_2_lt;
  wire [1:0] and_1_out;
  wire [31:0] adder_1_out, and_2_out, bit_extender_1_out, bit_extender_2_out, bit_extender_3_out,
       multiplexer_1_out, multiplexer_2_out, multiplication_1_r_high, multiplication_1_r_low, or_1_out,
       Source_1_q, Source_2_q, undriven, undriven_2, undriven_3, undriven_4, xor_1_out, xor_2_out;

  Multiplexer #(.width(32)) multiplexer_1 (
    .in0(Source1), .in1(Program_Counter_In), .out(multiplexer_1_out), .sel(Use_PC));
  Multiplexer #(.width(32)) multiplexer_2 (
    .in0(Source2), .in1(Immediate), .out(multiplexer_2_out), .sel(Use_Immediate));
  Register #(.trigger("falling"), .width(32)) Source_1 (
    .D(multiplexer_1_out), .en(Write), .clk(Clock), .Q(Source_1_q));  // open: clr
  Register #(.trigger("falling"), .width(32)) Source_2 (
    .D(multiplexer_2_out), .en(Write), .clk(Clock), .Q(Source_2_q));  // open: clr
  assign and_1_out = Operation[4:3] & ~{2{Use_Immediate}};  // AND_Gate and_1, 2 bits wide
  assign or_1_out = Source_1_q | Source_2_q;  // OR_Gate or_1, 32 bits wide
  assign and_2_out = Source_1_q & Source_2_q;  // AND_Gate and_2, 32 bits wide
  assign bit_extender_1_out = {{31{and_1_out[1]}}, and_1_out[1]};  // Bit_Extender bit_extender_1
  assign bit_extender_2_out = {{31{1'b0}}, comparator_1_lt};  // Bit_Extender bit_extender_2
  Comparator #(.width(32)) comparator_1 (.a(Source_1_q), .b(Source_2_q), .lt(comparator_1_lt));  // open: gt, eq
  assign bit_extender_3_out = {{31{1'b0}}, comparator_2_lt};  // Bit_Extender bit_extender_3
  Comparator #(.mode("unsigned"), .width(32)) comparator_2 (
    .a(Source_1_q), .b(Source_2_q), .lt(comparator_2_lt));  // open: gt, eq
  assign xor_1_out = Source_1_q ^ Source_2_q;  // XOR_Gate xor_1, 32 bits wide
  Multiplication multiplication_1 (
    .Sign(Operation[1:0]), .A(Source_1_q), .B(Source_2_q), .R_Low(multiplication_1_r_low),
    .R_High(multiplication_1_r_high));
  Adder #(.width(32)) adder_1 (.a(Source_1_q), .b(xor_2_out), .out(adder_1_out), .cin(and_1_out[1]), .cout(CNZV[0]));
  assign xor_2_out = bit_extender_1_out ^ Source_2_q;  // XOR_Gate xor_2, 32 bits wide
  Multiplexer #(.select(4), .width(32)) multiplexer_3 (
    .in0(adder_1_out), .in1({32{1'b0}}), .in2(bit_extender_2_out), .in3(bit_extender_3_out), .in4(xor_1_out),
    .in5({32{1'b0}}), .in6(or_1_out), .in7(and_2_out), .in8(multiplication_1_r_low),
    .in9(multiplication_1_r_high), .in10(multiplication_1_r_high), .in11(multiplication_1_r_high),
    .in12(undriven), .in13(undriven_2), .in14(undriven_3), .in15(undriven_4), .out({CNZV[1], Result[30:0]}),
    .sel({and_1_out[0], Operation[2:0]}));
  nor nor_1 (CNZV[2], Result[0], Result[1], Result[2], Result[3], Result[4], Result[5], Result[6], Result[7], Result[8], Result[9], Result[10], Result[11], Result[12], Result[13], Result[14], Result[15], Result[16], Result[17], Result[18], Result[19], Result[20], Result[21], Result[22], Result[23], Result[24], Result[25], Result[26], Result[27], Result[28], Result[29], Result[30], CNZV[1]);
  xor xor_3 (CNZV[3], CNZV[1], CNZV[0]);

  assign Result[31] = CNZV[1];

  // Notes on the sheet:
  //   Source1: initial=0xffffffff
endmodule

module Program_Counter (
  input  Write,
  input  Jump,
  input  Reset,
  input  Clock,
  input  [31:0] D_Bus_In,
  input  Use_Offset,
  input  D_Bus_To_AD,
  output [31:0] Last_Out,
  output [31:0] Current_Out,
  output [31:0] Next_Out,
  output [31:0] AD_Bus_Out,
  output [1:0] Byte_Offset
);

  wire [1:0] and_1_out;

  Counter #(.max('h3fffffff), .trigger("falling"), .width(30)) Next_Counter (
    .load(Jump), .D(D_Bus_In[31:2]), .count(Write), .Q(Next_Out[31:2]), .clk(Clock), .clr(Reset));  // open: carry, up
  assign and_1_out = D_Bus_In[1:0] & {2{Use_Offset}};  // AND_Gate and_1, 2 bits wide
  Register #(.trigger("falling"), .width(2)) Byte_Offset_Reg (
    .D(D_Bus_In[1:0]), .en(D_Bus_To_AD), .clk(Clock), .Q(Byte_Offset), .clr(Reset));
  Register #(.trigger("falling"), .width(30)) Current (
    .D(Next_Out[31:2]), .en(Write), .clk(Clock), .Q(Current_Out[31:2]), .clr(Reset));
  Multiplexer #(.width(32)) multiplexer_1 (
    .in0({Next_Out[31:2], 2'b00}), .in1({D_Bus_In[31:2], and_1_out}), .out(AD_Bus_Out), .sel(D_Bus_To_AD));
  Register #(.trigger("falling"), .width(30)) Last (
    .D(Current_Out[31:2]), .en(Write), .clk(Clock), .Q(Last_Out[31:2]), .clr(Reset));

  assign Current_Out[1:0] = 2'b00;
  assign Last_Out[1:0] = 2'b00;
  assign Next_Out[1:0] = 2'b00;
endmodule

module Data_Input_Output (
  input  [31:0] CPU_In,
  input  Store_CPU,
  input  [2:0] Data_Type,
  input  [1:0] Data_Offset,
  input  [31:0] IO_In,
  input  Write_IO,
  input  Clock,
  output [31:0] IO_Out,
  output [31:0] CPU_Out
);

  wire and_1_out, and_2_out, not_1_out;
  wire [7:0] Input_Register_q, Input_Register_q_2, Input_Register_q_3, Input_Register_q_4, multiplexer_1_out;
  wire [15:0] multiplexer_2_out, multiplexer_3_out;
  wire [31:0] bit_extender_1_out, bit_extender_2_out, multiplexer_4_out;

  Register #(.trigger("falling"), .width(32)) Output_Register (
    .D(CPU_In), .en(Store_CPU), .clk(Clock), .Q(IO_Out));  // open: clr
  Register #(.trigger("falling"), .width(32)) Input_Register (
    .D(IO_In), .en(Write_IO), .clk(Clock),
    .Q({Input_Register_q_4, Input_Register_q_3, Input_Register_q_2, Input_Register_q}));  // open: clr
  Multiplexer #(.select(2), .width(8)) multiplexer_1 (
    .in0(Input_Register_q), .in1(Input_Register_q_2), .in2(Input_Register_q_3), .in3(Input_Register_q_4),
    .out(multiplexer_1_out), .sel(Data_Offset));
  Multiplexer #(.width(16)) multiplexer_2 (
    .in0({Input_Register_q_2, Input_Register_q}), .in1({Input_Register_q_3, Input_Register_q_2}),
    .out(multiplexer_2_out), .sel(Data_Offset[0]));
  Multiplexer #(.width(16)) multiplexer_3 (
    .in0(multiplexer_2_out), .in1({Input_Register_q_4, Input_Register_q_3}), .out(multiplexer_3_out),
    .sel(Data_Offset[1]));
  not not_1 (not_1_out, Data_Type[2]);
  and and_1 (and_1_out, multiplexer_1_out[7], not_1_out);
  assign bit_extender_1_out = {{24{and_1_out}}, multiplexer_1_out};  // Bit_Extender bit_extender_1
  and and_2 (and_2_out, multiplexer_3_out[15], not_1_out);
  assign bit_extender_2_out = {{16{and_2_out}}, multiplexer_3_out};  // Bit_Extender bit_extender_2
  Multiplexer #(.width(32)) multiplexer_4 (
    .in0(bit_extender_1_out), .in1(bit_extender_2_out), .out(multiplexer_4_out), .sel(Data_Type[0]));
  Multiplexer #(.width(32)) multiplexer_5 (
    .in0(multiplexer_4_out),
    .in1({Input_Register_q_4, Input_Register_q_3, Input_Register_q_2, Input_Register_q}), .out(CPU_Out),
    .sel(Data_Type[1]));

  // Notes on the sheet:
  //   IO_In: initial=0xf2f2f2f2
  //   CPU_In: initial=0xe3e3e3e3
endmodule

module Register_File (
  input  [14:0] Addresses_In,
  input  [31:0] C_Bus_In,
  input  Write,
  input  Clock,
  input  Reset,
  output [31:0] A_Bus_Out,
  output [31:0] B_Bus_Out
);

  Register_Bank IntRegisterBank (
    .Address_A(Addresses_In[9:5]), .Address_B(Addresses_In[14:10]), .Data_In(C_Bus_In), .Clock(Clock),
    .Address_C(Addresses_In[4:0]), .Write_Enable(Write), .Reset(Reset), .A_Data_Out(A_Bus_Out),
    .B_Data_Out(B_Bus_Out));
endmodule

module Register_Bank (
  input  [4:0] Address_A,
  input  Reset,
  input  [31:0] Data_In,
  input  Clock,
  input  [4:0] Address_C,
  input  [4:0] Address_B,
  input  Write_Enable,
  output [31:0] A_Data_Out,
  output [31:0] B_Data_Out
);

  wire [31:0] decoder_1_out0, x1_q, x2_q, x3_q, x4_q, x5_q, x6_q, x7_q, x8_q, x9_q, x10_q, x11_q, x12_q,
       x13_q, x14_q, x15_q, x16_q, x17_q, x18_q, x19_q, x20_q, x21_q, x22_q, x23_q, x24_q, x25_q, x26_q,
       x27_q, x28_q, x29_q, x30_q, x31_q;

  Decoder #(.select(5)) decoder_1 (
    .out0(decoder_1_out0[0]), .out1(decoder_1_out0[1]), .out2(decoder_1_out0[2]), .out3(decoder_1_out0[3]),
    .out4(decoder_1_out0[4]), .out5(decoder_1_out0[5]), .out6(decoder_1_out0[6]), .out7(decoder_1_out0[7]),
    .out8(decoder_1_out0[8]), .out9(decoder_1_out0[9]), .out10(decoder_1_out0[10]),
    .out11(decoder_1_out0[11]), .out12(decoder_1_out0[12]), .out13(decoder_1_out0[13]),
    .out14(decoder_1_out0[14]), .out15(decoder_1_out0[15]), .out16(decoder_1_out0[16]),
    .out17(decoder_1_out0[17]), .out18(decoder_1_out0[18]), .out19(decoder_1_out0[19]),
    .out20(decoder_1_out0[20]), .out21(decoder_1_out0[21]), .out22(decoder_1_out0[22]),
    .out23(decoder_1_out0[23]), .out24(decoder_1_out0[24]), .out25(decoder_1_out0[25]),
    .out26(decoder_1_out0[26]), .out27(decoder_1_out0[27]), .out28(decoder_1_out0[28]),
    .out29(decoder_1_out0[29]), .out30(decoder_1_out0[30]), .out31(decoder_1_out0[31]), .sel(Address_C),
    .en(Write_Enable));
  // NoConnect on Data_In
  // NoConnect on decoder_1_out0[0]
  // NoConnect on Clock
  Register #(.trigger("falling"), .width(32)) x2 (
    .D(Data_In), .en(decoder_1_out0[2]), .clk(Clock), .Q(x2_q), .clr(Reset));
  Register #(.trigger("falling"), .width(32)) x4 (
    .D(Data_In), .en(decoder_1_out0[4]), .clk(Clock), .Q(x4_q), .clr(Reset));
  Register #(.trigger("falling"), .width(32)) x6 (
    .D(Data_In), .en(decoder_1_out0[6]), .clk(Clock), .Q(x6_q), .clr(Reset));
  Register #(.trigger("falling"), .width(32)) x8 (
    .D(Data_In), .en(decoder_1_out0[8]), .clk(Clock), .Q(x8_q), .clr(Reset));
  Register #(.trigger("falling"), .width(32)) x10 (
    .D(Data_In), .en(decoder_1_out0[10]), .clk(Clock), .Q(x10_q), .clr(Reset));
  Register #(.trigger("falling"), .width(32)) x12 (
    .D(Data_In), .en(decoder_1_out0[12]), .clk(Clock), .Q(x12_q), .clr(Reset));
  Register #(.trigger("falling"), .width(32)) x14 (
    .D(Data_In), .en(decoder_1_out0[14]), .clk(Clock), .Q(x14_q), .clr(Reset));
  Register #(.trigger("falling"), .width(32)) x16 (
    .D(Data_In), .en(decoder_1_out0[16]), .clk(Clock), .Q(x16_q), .clr(Reset));
  Register #(.trigger("falling"), .width(32)) x18 (
    .D(Data_In), .en(decoder_1_out0[18]), .clk(Clock), .Q(x18_q), .clr(Reset));
  Register #(.trigger("falling"), .width(32)) x20 (
    .D(Data_In), .en(decoder_1_out0[20]), .clk(Clock), .Q(x20_q), .clr(Reset));
  Register #(.trigger("falling"), .width(32)) x22 (
    .D(Data_In), .en(decoder_1_out0[22]), .clk(Clock), .Q(x22_q), .clr(Reset));
  Register #(.trigger("falling"), .width(32)) x24 (
    .D(Data_In), .en(decoder_1_out0[24]), .clk(Clock), .Q(x24_q), .clr(Reset));
  Register #(.trigger("falling"), .width(32)) x26 (
    .D(Data_In), .en(decoder_1_out0[26]), .clk(Clock), .Q(x26_q), .clr(Reset));
  Register #(.trigger("falling"), .width(32)) x28 (
    .D(Data_In), .en(decoder_1_out0[28]), .clk(Clock), .Q(x28_q), .clr(Reset));
  Register #(.trigger("falling"), .width(32)) x30 (
    .D(Data_In), .en(decoder_1_out0[30]), .clk(Clock), .Q(x30_q), .clr(Reset));
  Register #(.trigger("falling"), .width(32)) x1 (
    .D(Data_In), .en(decoder_1_out0[1]), .clk(Clock), .Q(x1_q), .clr(Reset));
  Register #(.trigger("falling"), .width(32)) x3 (
    .D(Data_In), .en(decoder_1_out0[3]), .clk(Clock), .Q(x3_q), .clr(Reset));
  Register #(.trigger("falling"), .width(32)) x5 (
    .D(Data_In), .en(decoder_1_out0[5]), .clk(Clock), .Q(x5_q), .clr(Reset));
  Register #(.trigger("falling"), .width(32)) x7 (
    .D(Data_In), .en(decoder_1_out0[7]), .clk(Clock), .Q(x7_q), .clr(Reset));
  Register #(.trigger("falling"), .width(32)) x9 (
    .D(Data_In), .en(decoder_1_out0[9]), .clk(Clock), .Q(x9_q), .clr(Reset));
  Register #(.trigger("falling"), .width(32)) x11 (
    .D(Data_In), .en(decoder_1_out0[11]), .clk(Clock), .Q(x11_q), .clr(Reset));
  Register #(.trigger("falling"), .width(32)) x13 (
    .D(Data_In), .en(decoder_1_out0[13]), .clk(Clock), .Q(x13_q), .clr(Reset));
  Register #(.trigger("falling"), .width(32)) x15 (
    .D(Data_In), .en(decoder_1_out0[15]), .clk(Clock), .Q(x15_q), .clr(Reset));
  Register #(.trigger("falling"), .width(32)) x17 (
    .D(Data_In), .en(decoder_1_out0[17]), .clk(Clock), .Q(x17_q), .clr(Reset));
  Register #(.trigger("falling"), .width(32)) x19 (
    .D(Data_In), .en(decoder_1_out0[19]), .clk(Clock), .Q(x19_q), .clr(Reset));
  Register #(.trigger("falling"), .width(32)) x21 (
    .D(Data_In), .en(decoder_1_out0[21]), .clk(Clock), .Q(x21_q), .clr(Reset));
  Register #(.trigger("falling"), .width(32)) x23 (
    .D(Data_In), .en(decoder_1_out0[23]), .clk(Clock), .Q(x23_q), .clr(Reset));
  Register #(.trigger("falling"), .width(32)) x25 (
    .D(Data_In), .en(decoder_1_out0[25]), .clk(Clock), .Q(x25_q), .clr(Reset));
  Register #(.trigger("falling"), .width(32)) x27 (
    .D(Data_In), .en(decoder_1_out0[27]), .clk(Clock), .Q(x27_q), .clr(Reset));
  Register #(.trigger("falling"), .width(32)) x29 (
    .D(Data_In), .en(decoder_1_out0[29]), .clk(Clock), .Q(x29_q), .clr(Reset));
  Register #(.trigger("falling"), .width(32)) x31 (
    .D(Data_In), .en(decoder_1_out0[31]), .clk(Clock), .Q(x31_q), .clr(Reset));
  Multiplexer #(.select(5), .width(32)) multiplexer_1 (
    .in0({32{1'b0}}), .in1(x1_q), .in2(x2_q), .in3(x3_q), .in4(x4_q), .in5(x5_q), .in6(x6_q), .in7(x7_q),
    .in8(x8_q), .in9(x9_q), .in10(x10_q), .in11(x11_q), .in12(x12_q), .in13(x13_q), .in14(x14_q),
    .in15(x15_q), .in16(x16_q), .in17(x17_q), .in18(x18_q), .in19(x19_q), .in20(x20_q), .in21(x21_q),
    .in22(x22_q), .in23(x23_q), .in24(x24_q), .in25(x25_q), .in26(x26_q), .in27(x27_q), .in28(x28_q),
    .in29(x29_q), .in30(x30_q), .in31(x31_q), .out(A_Data_Out), .sel(Address_A));
  Multiplexer #(.select(5), .width(32)) multiplexer_2 (
    .in0({32{1'b0}}), .in1(x1_q), .in2(x2_q), .in3(x3_q), .in4(x4_q), .in5(x5_q), .in6(x6_q), .in7(x7_q),
    .in8(x8_q), .in9(x9_q), .in10(x10_q), .in11(x11_q), .in12(x12_q), .in13(x13_q), .in14(x14_q),
    .in15(x15_q), .in16(x16_q), .in17(x17_q), .in18(x18_q), .in19(x19_q), .in20(x20_q), .in21(x21_q),
    .in22(x22_q), .in23(x23_q), .in24(x24_q), .in25(x25_q), .in26(x26_q), .in27(x27_q), .in28(x28_q),
    .in29(x29_q), .in30(x30_q), .in31(x31_q), .out(B_Data_Out), .sel(Address_B));
endmodule

module Operation_Controller (
  input  Phase1,
  input  Phase2,
  input  Phase3,
  input  [31:0] Data_In,
  input  Clock,
  input  Reset,
  input  [3:0] CNZV,
  output Address_ALU_Use_PC,
  output [14:0] Register_Adresses,
  output ALU_Use_PC,
  output [2:0] Funct3,
  output Register_File_Write,
  output Alu_Read,
  output Use_Immediate,
  output Shifter_Read,
  output [6:0] OPCode,
  output PC_Read_Next,
  output [4:0] OP_Function,
  output PC_Jump,
  output [31:0] Immediate,
  output Data_IO_Write_IO,
  output Data_IO_Read_IO,
  output IO_Load,
  output PC_Use_Offset,
  output PC_Addr_In_to_AD,
  output PAD_Read,
  output PAD_Write,
  output PAD_Read_Address,
  output Load_Upper_Immediate,
  output [1:0] PAD_Data_Size
);

  wire ALU, and_1_out, and_2_out, and_3_out, and_6_out, and_10_out, and_11_out, and_12_out, and_13_out,
       and_14_out, Branch, Floating_Point, Flush_Next_Instruction, Immediate_t, Jump_PC_Relative,
       Jump_Register_Relative, Load, Load_Second_Part, Load_Upper_Immediate_t, multiplexer_4_out, not_1_out,
       not_2_out, not_3_out, Operation, or_1_out, or_2_out, or_3_out, or_5_out, or_6_out, or_8_out,
       or_11_out, or_12_out, s_r_ff_1_qn, Shifter, Store_Second_Part, System, xor_1_out;
  wire [4:0] multiplexer_5_out;
  wire [4:4] not_4_out;
  wire [6:0] Funct7;
  wire [31:0] Last_Instruction_q, multiplexer_1_out, Next_Instruction_q;
  wire [31:7] Current_Instruction_q;

  Register #(.trigger("falling"), .width(32)) Next_Instruction (
    .D(Data_In), .en(Phase2), .clk(Clock), .Q(Next_Instruction_q), .clr(Reset));
  S_R_Flip_Flop s_r_ff_1 (
    .S(Flush_Next_Instruction), .R(Phase2), .clk(Clock), .Qn(s_r_ff_1_qn));  // open: Q, reset, preset
  Multiplexer #(.width(32)) multiplexer_1 (
    .in0(32'h13), .in1(Next_Instruction_q), .out(multiplexer_1_out), .sel(s_r_ff_1_qn));
  Register #(.width(32)) Current_Instruction (
    .D(multiplexer_1_out), .en(Phase1), .clk(Clock), .Q({Current_Instruction_q, OPCode}), .clr(Reset));
  Register #(.width(32)) Last_Instruction (
    .D({Current_Instruction_q, OPCode}), .en(Phase1), .clk(Clock), .Q(Last_Instruction_q), .clr(Reset));
  Multiplexer #(.width(15)) multiplexer_2 (
    .in0({Current_Instruction_q[24:15], Current_Instruction_q[11:7]}),
    .in1({Last_Instruction_q[24:15], Last_Instruction_q[11:7]}), .out(Register_Adresses), .sel(and_1_out));
  and and_1 (and_1_out, Load_Second_Part, Phase2);
  or or_1 (or_1_out, and_1_out, and_2_out);
  and and_2 (and_2_out, Store_Second_Part, Phase1);
  Multiplexer #(.width(10)) multiplexer_3 (
    .in0({Current_Instruction_q[31:25], Current_Instruction_q[14:12]}),
    .in1({Last_Instruction_q[31:25], Last_Instruction_q[14:12]}), .out({Funct7, Funct3}), .sel(or_1_out));
  or or_2 (or_2_out, ALU_Use_PC, Load_Upper_Immediate_t);
  Load_Store_Decoder LoadStoreDecoder (
    .OPCODE(Last_Instruction_q[6:0]), .STORE(Store_Second_Part), .LOAD(Load_Second_Part));
  Operation_Decoder OperationDecoder (
    .OPCODE(OPCode), .IMMEDIATE(Immediate_t), .LOAD(Load), .OPERATION(Operation),
    .ADD_UPPER_IMMEDIATE_PC(ALU_Use_PC), .STORE(PC_Use_Offset),
    .LOAD_UPPER_IMMEDIATE(Load_Upper_Immediate_t), .BRANCH(Branch),
    .JUMP_AND_LINK_REGISTER(Jump_Register_Relative), .JUMP_AND_LINK(Jump_PC_Relative), .SYSTEM(System),
    .FLOATING_POINT(Floating_Point));
  Immediate_Decoder ImmediateDecoder (
    .Upper_Immediate(or_2_out), .Jump(Jump_PC_Relative), .Branch(Branch),
    .Instruction({Current_Instruction_q, OPCode}), .Store(PC_Use_Offset), .Immediate(Immediate));
  or or_3 (or_3_out, Load_Upper_Immediate_t, ALU_Use_PC, Operation, Load, Jump_PC_Relative, Jump_Register_Relative, System);
  and and_3 (and_3_out, Phase3, or_3_out);
  or or_4 (Register_File_Write, and_3_out, and_6_out);
  or or_5 (or_5_out, Jump_Register_Relative, Jump_PC_Relative);
  and and_4 (PC_Read_Next, or_5_out, Phase3);
  xor xor_1 (xor_1_out, CNZV[3], CNZV[1]);
  or or_6 (or_6_out, Load, PC_Use_Offset);
  and and_5 (PC_Addr_In_to_AD, or_6_out, Phase3);
  and and_6 (and_6_out, Phase2, Load_Second_Part);
  not not_1 (not_1_out, CNZV[2]);
  not not_2 (not_2_out, xor_1_out);
  Multiplexer #(.enable("true"), .select(3)) multiplexer_4 (
    .in0(CNZV[2]), .in1(not_1_out), .in2(1'b0), .in3(1'b0), .in4(not_2_out), .in5(xor_1_out),
    .in6(not_3_out), .in7(CNZV[0]), .out(multiplexer_4_out), .sel(Funct3), .en(Branch));
  not not_3 (not_3_out, CNZV[0]);
  and and_7 (Load_Upper_Immediate, Load_Upper_Immediate_t, Phase3);
  or or_7 (Flush_Next_Instruction, multiplexer_4_out, Jump_Register_Relative, Jump_PC_Relative);
  or or_8 (or_8_out, Branch, ALU_Use_PC, ALU);
  and and_8 (Alu_Read, Phase3, or_8_out);
  and and_9 (PC_Jump, Flush_Next_Instruction, Phase3);
  not not_4 (not_4_out[4], Funct3[2]);
  or or_9 (Use_Immediate, Immediate_t, ALU_Use_PC);
  and and_10 (and_10_out, Operation, ~Load_Second_Part);  // AND_Gate
  Multiplexer #(.width(5)) multiplexer_5 (
    .in0({not_4_out[4], 4'b0101}), .in1(5'b10000), .out(multiplexer_5_out), .sel(Branch));
  Multiplexer #(.width(5)) multiplexer_6 (
    .in0(multiplexer_5_out), .in1({Funct7[5], Funct7[1], Funct3}), .out(OP_Function), .sel(and_10_out));
  or or_10 (Address_ALU_Use_PC, Branch, Jump_PC_Relative);
  or or_11 (or_11_out, OP_Function[2], ~OP_Function[4]);  // OR_Gate
  or or_12 (or_12_out, Load, PC_Use_Offset);
  and and_11 (and_11_out, OP_Function[0], ~OP_Function[1], ~OP_Function[3], or_11_out);  // AND_Gate
  and and_12 (and_12_out, or_12_out, Phase3);
  or or_13 (PAD_Read_Address, and_12_out, Phase1);
  and and_13 (and_13_out, Phase3, Shifter);
  or or_14 (Shifter_Read, and_13_out, and_14_out);
  Decoder decoder_1 (.out0(ALU), .out1(Shifter), .sel(and_11_out), .en(Operation));
  and and_14 (and_14_out, Phase2, Load_Second_Part);
  and and_15 (Data_IO_Write_IO, Phase1, Load_Second_Part);
  or or_15 (PAD_Read, Phase2, Data_IO_Write_IO);
  and and_16 (Data_IO_Read_IO, Phase1, Store_Second_Part);
  or or_16 (PAD_Data_Size[0], Funct3[0], Funct3[1]);
  and and_17 (IO_Load, Phase2, Load_Second_Part);

  assign PAD_Data_Size[1] = Funct3[1];
  assign PAD_Write = Data_IO_Read_IO;

  // Other names for the same wires on the sheet: Funct10[9:0] = {Funct7, Funct3}; Add_Upper_Immediate_PC = ALU_Use_PC;
  //   Phase1n = Phase1; Phase2n = Phase2; Phase3n = Phase3; Store = PC_Use_Offset

  // Notes on the sheet:
  //   Register File
  //   Program Counter
  //   Misc
  //   ALU And Shifter
  //   Input/Output and interface Pads
endmodule

module Operation_Decoder (
  input  [6:0] OPCODE,
  output FLOATING_POINT,
  output IMMEDIATE,
  output LOAD,
  output OPERATION,
  output ADD_UPPER_IMMEDIATE_PC,
  output STORE,
  output LOAD_UPPER_IMMEDIATE,
  output BRANCH,
  output JUMP_AND_LINK_REGISTER,
  output JUMP_AND_LINK,
  output SYSTEM
);

  wire not_1_out, not_2_out, not_3_out, not_4_out, not_5_out, or_1_out, or_2_out, or_3_out, or_4_out;

  not not_1 (not_1_out, OPCODE[6]);
  not not_2 (not_2_out, OPCODE[5]);
  not not_3 (not_3_out, OPCODE[4]);
  not not_4 (not_4_out, OPCODE[3]);
  not not_5 (not_5_out, OPCODE[2]);
  or or_1 (or_1_out, OPCODE[6], not_3_out);
  or or_2 (or_2_out, not_1_out, not_2_out);
  or or_3 (or_3_out, OPCODE[4], OPCODE[2]);
  and and_1 (IMMEDIATE, not_2_out, not_1_out, not_5_out);
  and and_2 (LOAD, not_3_out, not_2_out);
  or or_4 (or_4_out, not_1_out, not_2_out);
  and and_3 (ADD_UPPER_IMMEDIATE_PC, OPCODE[2], OPCODE[4], not_2_out);
  and and_4 (STORE, OPCODE[5], not_3_out, not_1_out);
  and and_5 (LOAD_UPPER_IMMEDIATE, OPCODE[2], OPCODE[5], OPCODE[4]);
  and and_6 (BRANCH, OPCODE[6], not_3_out, not_5_out);
  and and_7 (JUMP_AND_LINK_REGISTER, OPCODE[2], not_4_out, OPCODE[6]);
  and and_8 (JUMP_AND_LINK, OPCODE[3], OPCODE[6]);
  and and_9 (SYSTEM, OPCODE[6], OPCODE[5], OPCODE[4]);
  and and_10 (FLOATING_POINT, or_1_out, or_2_out, or_3_out);
  and and_11 (OPERATION, OPCODE[4], or_4_out, not_5_out);
endmodule

module Immediate_Decoder (
  input  Upper_Immediate,
  input  Jump,
  input  Branch,
  input  Store,
  input  [31:0] Instruction,
  output [31:0] Immediate
);

  wire [1:0] or_2_out;
  wire [11:0] multiplexer_1_out;
  wire [31:0] bit_extender_1_out, bit_extender_2_out, bit_extender_3_out;

  Multiplexer #(.width(12)) multiplexer_1 (
    .in0(Instruction[31:20]), .in1({Instruction[31:25], Instruction[11:7]}), .out(multiplexer_1_out),
    .sel(Store));
  assign bit_extender_1_out = {{19{Instruction[31]}}, {Instruction[31], Instruction[7], Instruction[30:25], Instruction[11:8], 1'b0}};  // Bit_Extender bit_extender_1
  assign bit_extender_2_out = {{11{Instruction[31]}}, {Instruction[31], Instruction[19:12], Instruction[20], Instruction[30:21], 1'b0}};  // Bit_Extender bit_extender_2
  assign bit_extender_3_out = {{20{multiplexer_1_out[11]}}, multiplexer_1_out};  // Bit_Extender bit_extender_3
  or or_1 (or_2_out[1], Upper_Immediate, Jump);
  or or_2 (or_2_out[0], Jump, Branch);
  Multiplexer #(.select(2), .width(32)) multiplexer_2 (
    .in0(bit_extender_3_out), .in1(bit_extender_1_out), .in2({Instruction[31:12], {12{1'b0}}}),
    .in3(bit_extender_2_out), .out(Immediate), .sel(or_2_out));

  // Notes on the sheet:
  //   I-type
  //   S-type
  //   B-type
  //   U-type
  //   J-type
endmodule

module Load_Store_Decoder (
  input  [6:0] OPCODE,
  output LOAD,
  output STORE
);

  wire and_2_out, and_3_out, not_1_out, not_2_out, not_3_out, not_4_out, not_5_out;

  not not_1 (not_1_out, OPCODE[6]);
  not not_2 (not_2_out, OPCODE[5]);
  not not_3 (not_3_out, OPCODE[4]);
  not not_4 (not_4_out, OPCODE[3]);
  not not_5 (not_5_out, OPCODE[2]);
  and and_1 (LOAD, not_1_out, not_2_out, not_3_out, not_4_out, OPCODE[1], OPCODE[0]);
  and and_2 (and_2_out, not_1_out, OPCODE[5], not_3_out, not_4_out, not_5_out, OPCODE[1], OPCODE[0]);
  and and_3 (and_3_out, not_1_out, OPCODE[5], not_3_out, OPCODE[3], OPCODE[2], OPCODE[1], OPCODE[0]);
  or or_1 (STORE, and_2_out, and_3_out);
endmodule

module IO_Controller (
  input  [31:0] Keyboard_Address,
  input  [31:0] Video_Address,
  input  [31:0] Address_In,
  input  Write_Address,
  input  Clock,
  input  Reset,
  input  Read,
  input  Write,
  output [31:0] AddressDebug,
  output Read_Keyboard,
  output Write_Video,
  output [23:0] Address_Out_24Bit,
  output ReadRam,
  output Read_OS_Ram,
  output [7:0] Rom_Address_Out_8Bit,
  output WriteRam,
  output Write_OS_Ram
);

  wire comparator_1_eq, comparator_2_eq, decoder_1_out0, decoder_1_out1, decoder_2_out0, decoder_2_out1,
       decoder_2_out2;

  Register #(.trigger("falling"), .width(32)) Memory_Address (
    .D(Address_In), .en(Write_Address), .clk(Clock), .Q({AddressDebug[31:24], Address_Out_24Bit}), .clr(Reset));
  Comparator #(.width(32)) comparator_1 (
    .a(Keyboard_Address), .b({AddressDebug[31:24], Address_Out_24Bit}), .eq(comparator_1_eq));  // open: gt, lt
  Comparator #(.width(32)) comparator_2 (
    .a(Video_Address), .b({AddressDebug[31:24], Address_Out_24Bit}), .eq(comparator_2_eq));  // open: gt, lt
  Decoder #(.select(2)) decoder_1 (
    .out0(decoder_1_out0), .out1(decoder_1_out1), .out3(Write_OS_Ram), .sel(AddressDebug[31:30]), .en(Write));  // open: out2
  and and_1 (Read_Keyboard, comparator_1_eq, Read);
  and and_2 (Write_Video, comparator_2_eq, Write);
  or or_1 (WriteRam, decoder_1_out0, decoder_1_out1);
  Decoder #(.select(2)) decoder_2 (
    .out0(decoder_2_out0), .out1(decoder_2_out1), .out2(decoder_2_out2), .out3(Read_OS_Ram),
    .sel(AddressDebug[31:30]), .en(Read));
  or or_2 (ReadRam, decoder_2_out0, decoder_2_out1);
  assign Rom_Address_Out_8Bit = decoder_2_out2 ? Address_Out_24Bit[9:2] : 8'bz;  // Controlled_Buffer controlled_buffer_1

  assign AddressDebug[23:0] = Address_Out_24Bit;
endmodule

module Register_History_Generator (
  input  [31:0] Current_Value,
  input  [4:0] Current_Address,
  input  [4:0] Target_Address,
  input  Write_Signal,
  input  Reset,
  input  Clock,
  output Out_Clock,
  output [15:0] Out_Value
);

  wire and_1_out, comparator_1_eq, comparator_2_gt;
  wire [3:0] counter_1_q;
  wire [31:0] Last_Value_q, register_1_q;

  Comparator #(.width(5)) comparator_1 (.a(Current_Address), .b(Target_Address), .eq(comparator_1_eq));  // open: gt, lt
  and and_1 (and_1_out, comparator_1_eq, Write_Signal);
  Register #(.trigger("falling"), .width(32)) register_1 (
    .D(Current_Value), .en(and_1_out), .clk(Clock), .Q(register_1_q));  // open: clr
  Register #(.trigger("falling"), .width(32)) Last_Value (
    .D(Current_Value), .en(and_1_out), .clk(Clock), .Q(Last_Value_q), .clr(Reset));
  and and_2 (Out_Clock, and_1_out, Clock);
  Comparator #(.width(32)) comparator_2 (.a(register_1_q), .b(Last_Value_q), .gt(comparator_2_gt));  // open: eq, lt
  Counter #(.max('hf), .width(4)) counter_1 (
    .clr(Reset), .up(comparator_2_gt), .count(and_1_out), .clk(Clock), .Q(counter_1_q));  // open: load, D, carry
  Decoder #(.enable("false"), .select(4)) decoder_1 (
    .out0(Out_Value[0]), .out1(Out_Value[1]), .out2(Out_Value[2]), .out3(Out_Value[3]), .out4(Out_Value[4]),
    .out5(Out_Value[5]), .out6(Out_Value[6]), .out7(Out_Value[7]), .out8(Out_Value[8]), .out9(Out_Value[9]),
    .out10(Out_Value[10]), .out11(Out_Value[11]), .out12(Out_Value[12]), .out13(Out_Value[13]),
    .out14(Out_Value[14]), .out15(Out_Value[15]), .sel(counter_1_q));
endmodule

module F_ALU (
  input  [4:0] Operation,
  input  Write,
  input  Use_PC,
  input  [31:0] Source1,
  input  [31:0] Program_Counter_In,
  input  Use_Immediate,
  input  [31:0] Source2,
  input  [31:0] Immediate,
  input  Clock,
  input  in_10,
  output [31:0] Result,
  output [3:0] CNZV
);

  wire fpcomparator_1_p5, fpcomparator_1_p10, fpcomparator_1_p11, xor_1_out;
  wire [1:0] and_1_out;
  wire [7:0] slider_1_out, slider_2_out;
  wire [15:0] bit_extender_1_out, bit_extender_2_out;
  wire [31:0] fpcomparator_1_p4, fpcomparator_1_p8, fpcomparator_1_p9, inttofp_1_p2, inttofp_2_p2,
       multiplexer_1_out, multiplexer_2_out, multiplexer_3_out, multiplexer_4_out, Source_1_q, Source_2_q,
       undriven, undriven_2, undriven_3, undriven_4, undriven_5, undriven_6, undriven_7, undriven_8,
       undriven_9, undriven_10, undriven_11, undriven_12;

  Multiplexer #(.width(32)) multiplexer_1 (
    .in0(Source1), .in1(Program_Counter_In), .out(multiplexer_1_out), .sel(Use_PC));
  Multiplexer #(.width(32)) multiplexer_2 (
    .in0(Source2), .in1(Immediate), .out(multiplexer_2_out), .sel(Use_Immediate));
  Register #(.trigger("falling"), .width(32)) Source_1 (
    .D(multiplexer_1_out), .en(Write), .clk(Clock), .Q(Source_1_q));  // open: clr
  Register #(.trigger("falling"), .width(32)) Source_2 (
    .D(multiplexer_2_out), .en(Write), .clk(Clock), .Q(Source_2_q));  // open: clr
  assign bit_extender_1_out = {{8{1'b0}}, slider_1_out};  // Bit_Extender bit_extender_1
  Slider slider_1 (.out(slider_1_out));
  assign bit_extender_2_out = {{8{1'b0}}, slider_2_out};  // Bit_Extender bit_extender_2
  Slider slider_2 (.out(slider_2_out));
  // IntToFP #(.width(16)) inttofp_1: pin names not known; wires that end beside it: bit_extender_1_out, inttofp_1_p2
  // IntToFP #(.width(16)) inttofp_2: pin names not known; wires that end beside it: bit_extender_2_out, inttofp_2_p2
  // FPComparator fpcomparator_1: pin names not known; wires that end beside it: Source_2_q, Source_1_q, Source_2_q, fpcomparator_1_p4, fpcomparator_1_p5, inttofp_1_p2, inttofp_2_p2, fpcomparator_1_p8, fpcomparator_1_p9, fpcomparator_1_p10, fpcomparator_1_p11
  Multiplexer #(.width(32)) multiplexer_3 (
    .in0(inttofp_1_p2), .in1(inttofp_2_p2), .out(multiplexer_3_out), .sel(xor_1_out));
  xor xor_1 (xor_1_out, fpcomparator_1_p10, in_10);
  FPDivider fpdivider_1 ();  // open: a, b, out
  // Probe on multiplexer_3_out
  FPSubtractor fpsubtractor_1 ();  // open: a, b, out
  FPMultiplier fpmultiplier_1 ();  // open: a, b, out
  // FPToInt fptoint_1: pin names not known
  assign and_1_out = Operation[4:3] & ~{2{Use_Immediate}};  // AND_Gate and_1, 2 bits wide
  FPAdder fpadder_1 ();  // open: a, b, out
  Multiplexer #(.select(4), .width(32)) multiplexer_4 (
    .in0(undriven_2), .in1({32{1'b0}}), .in2(undriven), .in3(undriven_3), .in4(undriven_4), .in5({32{1'b0}}),
    .in6(undriven_5), .in7(undriven_6), .in8(undriven_7), .in9(undriven_8), .in10(undriven_9),
    .in11(undriven_10), .in12(undriven_11), .in13(fpcomparator_1_p8), .in14(undriven_12),
    .in15(fpcomparator_1_p4), .out(multiplexer_4_out), .sel({and_1_out[0], Operation[2:0]}));
  Multiplexer #(.width(32)) multiplexer_5 (
    .in0(multiplexer_4_out), .in1(fpcomparator_1_p9), .out({CNZV[1], Result[30:0]}), .sel(and_1_out[1]));
  Multiplexer multiplexer_6 (.in0(fpcomparator_1_p11), .in1(fpcomparator_1_p5), .out(CNZV[0]), .sel(and_1_out[1]));
  nor nor_1 (CNZV[2], Result[0], Result[1], Result[2], Result[3], Result[4], Result[5], Result[6], Result[7], Result[8], Result[9], Result[10], Result[11], Result[12], Result[13], Result[14], Result[15], Result[16], Result[17], Result[18], Result[19], Result[20], Result[21], Result[22], Result[23], Result[24], Result[25], Result[26], Result[27], Result[28], Result[29], Result[30], CNZV[1]);
  xor xor_2 (CNZV[3], CNZV[1], CNZV[0]);

  assign Result[31] = CNZV[1];

  // Notes on the sheet:
  //   Source1: initial=0xffffffff
endmodule

module Multiplication (
  input  [31:0] A,
  input  [31:0] B,
  input  [1:0] Sign,
  output [31:0] R_Low,
  output [31:0] R_High
);

  wire [32:31] multiplier_1_cout;
  wire [32:32] and_1_out, and_2_out;

  and and_1 (and_1_out[32], A[31], Sign[0]);
  and and_2 (and_2_out[32], B[31], Sign[1]);
  Multiplier #(.mode("twosComplement"), .width(33)) multiplier_1 (
    .a({and_1_out[32], A}), .b({and_2_out[32], B}), .out({R_High[0], R_Low}),
    .cout({multiplier_1_cout, R_High[31:1]}));  // open: cin
endmodule
